// Logisim project porteslogiques2809.circ as structural Verilog: 1 circuit, main circuit main
module main (
  input  A,
  input  B,
  input  C,
  input  E1,
  input  C_2,
  input  E2,
  input  A_2,
  input  B_2,
  output S,
  output OUT,
  output S_2,
  output C_3
);

  wire and_1_out, AND_2_out, AND_3_out, not_1_out, or_1_out;

  not not_1 (not_1_out, C_2);
  or or_1 (or_1_out, A, B);
  buf and_1 (and_1_out, C);  // AND_Gate
  and AND_2 (AND_2_out, E1, not_1_out);
  and AND_3 (AND_3_out, C_2, E2);
  or XOR (S_2, A_2, B_2);
  and AND_4 (C_3, A_2, B_2);
  or or_2 (S, or_1_out, and_1_out);
  or OU (OUT, AND_2_out, AND_3_out);
endmodule
